# Fritzing sketch ergoFACE_prototype_concept (saved by Fritzing 0.9.3b)
breadboards: 1

parts:
  Raspberry_Pi_1 = Raspberry Pi 3 [part_number=RPI-3-V1.2]
  J2 = Camdenboss CTB0158-4 [part_number=CTB0158-4 package=THT]

nets:
  N1: Raspberry_Pi_1.GPIO24, J2.pin4
  N2: Raspberry_Pi_1.GND, J2.pin2

notes:
  +5V
  GND
  RPM
  BRK
